// Logisim project 16-bit Computer.circ as structural Verilog: 2 circuits, main circuit main
module main (
  input  Power,
  input  Manual_Override,
  input  in_3,
  input  in_4,
  input  in_5,
  input  in_6,
  input  in_7,
  input  in_8,
  input  in_9,
  output out_10,
  output out_11,
  output out_12,
  output out_13,
  output out_14,
  output out_15,
  output out_16,
  output out_17,
  output out_18,
  output out_19,
  output out_20,
  output out_21,
  output out_22,
  output out_23,
  output out_24,
  output out_25
);

  wire Clock_out, Manual_Tick_out;
  wire [15:0] and_1_out, and_2_out, and_3_out, and_4_out, and_5_out, AX_q, BX_q, CX_q, DX_q, MAR_q, or_2_out,
       ram_1_data;
  wire [15:15] rom_1_data, rom_1_data_2, rom_1_data_3, rom_1_data_4;

  Button Manual_Tick (.out(Manual_Tick_out));
  Clock Clock (.Power(Power), .Manual_Override(Manual_Override), .Manual_Tick(Manual_Tick_out), .Out(Clock_out));
  assign {out_10, out_11, out_12, out_13, out_14, out_15, out_16, out_17, out_18, out_19, out_20, out_21, out_22, out_23, out_24, out_25} = and_5_out | or_2_out;  // OR_Gate or_1, 16 bits wide
  assign or_2_out = and_1_out | and_2_out | and_3_out | and_4_out;  // OR_Gate or_2, 16 bits wide
  Register #(.width(16)) MAR (
    .D({out_10, out_11, out_12, out_13, out_14, out_15, out_16, out_17, out_18, out_19, out_20, out_21, out_22, out_23, out_24, out_25}),
    .en(in_9), .Q(MAR_q), .clk(Clock_out));  // open: clr
  assign and_1_out = {16{rom_1_data[15]}} & DX_q;  // AND_Gate and_1, 16 bits wide
  assign and_2_out = {16{rom_1_data_2[15]}} & CX_q;  // AND_Gate and_2, 16 bits wide
  assign and_3_out = {16{rom_1_data_3[15]}} & BX_q;  // AND_Gate and_3, 16 bits wide
  assign and_4_out = {16{rom_1_data_4[15]}} & AX_q;  // AND_Gate and_4, 16 bits wide
  Register #(.width(16)) AX (
    .D({out_10, out_11, out_12, out_13, out_14, out_15, out_16, out_17, out_18, out_19, out_20, out_21, out_22, out_23, out_24, out_25}),
    .en(in_3), .Q(AX_q), .clk(Clock_out));  // open: clr
  assign and_5_out = ram_1_data;  // AND_Gate and_5, 16 bits wide AND_Gate
  Register #(.width(16)) BX (
    .D({out_10, out_11, out_12, out_13, out_14, out_15, out_16, out_17, out_18, out_19, out_20, out_21, out_22, out_23, out_24, out_25}),
    .en(in_4), .Q(BX_q), .clk(Clock_out));  // open: clr
  RAM #(.addrWidth(16), .dataWidth(16), .bus("separate")) ram_1 (
    .addr(MAR_q),
    .din({out_10, out_11, out_12, out_13, out_14, out_15, out_16, out_17, out_18, out_19, out_20, out_21, out_22, out_23, out_24, out_25}),
    .data(ram_1_data));  // open: str, sel, clk, ld, clr
  Register #(.width(16)) CX (
    .D({out_10, out_11, out_12, out_13, out_14, out_15, out_16, out_17, out_18, out_19, out_20, out_21, out_22, out_23, out_24, out_25}),
    .en(in_5), .Q(CX_q), .clk(Clock_out));  // open: clr
  Register #(.width(16)) DX (
    .D({out_10, out_11, out_12, out_13, out_14, out_15, out_16, out_17, out_18, out_19, out_20, out_21, out_22, out_23, out_24, out_25}),
    .en(in_6), .Q(DX_q), .clk(Clock_out));  // open: clr
  ROM #(.addrWidth(2), .dataWidth(4)) rom_1 (
    .addr({in_8, in_7}), .data({rom_1_data[15], rom_1_data_2[15], rom_1_data_3[15], rom_1_data_4[15]}));  // open: sel

  // Notes on the sheet:
  //   contents of rom_1 (hex, n*v repeats v):
  //   1 2 4 8
endmodule

module Clock (
  input  Power,
  input  Manual_Override,
  input  Manual_Tick,
  output Out
);

  wire and_1_out, and_2_out, clock_1_out, not_1_out, or_1_out;

  Clock_part clock_1 (.out(clock_1_out));
  not not_1 (not_1_out, Manual_Override);
  and and_1 (and_1_out, not_1_out, clock_1_out);
  and and_2 (and_2_out, Manual_Override, Manual_Tick);
  or or_1 (or_1_out, and_1_out, and_2_out);
  and and_3 (Out, Power, or_1_out);
endmodule
